# Fritzing sketch Schematy (saved by Fritzing 1.0.6)
breadboards: 1

parts:
  Akcelerometr_(LIS3DHTR) = Grove 3 Axis Digital Accelerometer 16g
  Przycisk = Grove Button
  Buzzer = Grove Buzz
  Potencjometr = Grove Rotary Angle Sensor
  LED1 = smd LED [color="Red (633nm)" package="0603 [SMD]"]
  R1 = Resistor [tolerance=±5% power=0.25W resistance=220 package=THT]
  OLED_(SSD1315) = Grove 3 Axis Digital Accelerometer 16g
  Arduino_Uno = Arduino Uno (Rev3) - ICSP

nets:
  GND: Akcelerometr_(LIS3DHTR).GND, Przycisk.GND, Buzzer.GND, Potencjometr.GND, LED1.cathode, OLED_(SSD1315).GND, Arduino_Uno.GND
  5V: Akcelerometr_(LIS3DHTR).VCC, Przycisk.VCC, Buzzer.VCC, Potencjometr.VCC, OLED_(SSD1315).VCC, Arduino_Uno.5V
  N1: Akcelerometr_(LIS3DHTR).SDA, Arduino_Uno.A4/SDA
  N2: Akcelerometr_(LIS3DHTR).SCL, Arduino_Uno.A5/SCL
  N3: Przycisk.SIG, Arduino_Uno.D6_PWM
  N4: Buzzer.SIG, Arduino_Uno.D5_PWM
  N5: Potencjometr.SIG, Arduino_Uno.A0
  N6: LED1.anode, R1.Pin_1
  N7: R1.Pin_0, Arduino_Uno.D4

custom parts:
  Grove Rotary Angle Sensor: A potentiometer
